# Fritzing sketch wiring (saved by Fritzing 1.0.2b)
perfboards: 1

parts:
  Adafruit_RP2040_Prop-Maker_Feather1 = Adafruit RP2040 Prop-Maker Feather [part_number=#5768]
  R1 = Slide Potentiometer [maximum_resistance=100kΩ knob_status=50% power=0.5W]
  U1 = POT [knob_status=50% power=0.5W package=pot_mammoth]
  Part1 = Adafruit MAX4466 Electret Microphone Amplifier [part_number="Adafruit #1063"]
  NEOPIXEL1 = Neopixel Strip -- White (30/m)
  LED1 = RGB LED (com. anode, rbg) [color="Red (633nm)" current=0.030A package="5 mm [THT]"]
  S1 = Round Pushbutton
  J1 = JST-03JQ-BT [part_number=JST-JQ-BT package=THT]
  J2 = JST-03JQ-BT [part_number=JST-JQ-BT package=THT]
  J4 = Screw terminal - 2 pins [package=THT]
  Power_plug1 = USB-C plug
  J5 = JST-03JQ-BT [part_number=JST-JQ-BT package=THT]
  U2 = JST XH 4A 2.54mm [package=THT]
  U3 = SWITCH_SPDT [package=kps-1290]

nets:
  N1: Adafruit_RP2040_Prop-Maker_Feather1.A0, R1.leg1, J2.pin3
  GND: Adafruit_RP2040_Prop-Maker_Feather1.GND, NEOPIXEL1.GND, S1.leg0, J4.pin2, Power_plug1.GND, U3.O
  N2: Adafruit_RP2040_Prop-Maker_Feather1.+3V3, LED1.common_anode, U2.pin4
  N3: Adafruit_RP2040_Prop-Maker_Feather1.EN, U3.P
  N4: Adafruit_RP2040_Prop-Maker_Feather1.VBUS, J4.pin1, Power_plug1.VCC
  N5: Adafruit_RP2040_Prop-Maker_Feather1.PIXELOUT, NEOPIXEL1.Din
  N6: Adafruit_RP2040_Prop-Maker_Feather1.V+, NEOPIXEL1.+5V
  N7: Adafruit_RP2040_Prop-Maker_Feather1.BUTTON, S1.leg1
  N8: R1.wiper, J2.pin2
  N9: R1.leg2, J2.pin1
  N10: U1.S, J1.pin1
  N11: U1.A, J1.pin3
  N12: U1.E, J1.pin2
  N13: Part1.VCC, J5.pin1
  N14: Part1.GND, J5.pin2
  N15: Part1.OUT, J5.pin3
  N16: LED1.red_cathode, U2.pin3
  N17: LED1.blue_cathode, U2.pin2
  N18: LED1.green_cathode, U2.pin1

custom parts:
  Adafruit RP2040 Prop-Maker Feather: The Adafruit Feather series gives you lots of options for a small, portable, rechargeable microcontroller board. By picking a feather and stacking on a FeatherWing you can create advanced projects quickly. One popular combo is our Feather M4 or Feather RP2040 with a Prop-Maker FeatherWing on top to create animatronics or props that boot up instantly and can drive LEDs, and small speakers.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
  Adafruit MAX4466 Electret Microphone Amplifier: Add an ear to your project with this well-designed electret microphone amplifier. This fully assembled and tested board comes with a 20-20KHz electret microphone soldered on. For the amplification, we use the Maxim MAX4466, an op-amp specifically designed for this delicate task! The amplifier has excellent power supply noise rejection, so this amplifier sounds really good and isn't nearly as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
  Neopixel Strip -- White (30/m): These NeoPixel strips have 30 digitally-addressable pixel LEDs per meter and are very affordable and are only 12.5 mm wide, 10 mm if you remove the strip from the casing.
  USB-C plug: power plug
  JST XH 4A 2.54mm: 4 Pin JST XH connector
